// Logisim project 32-bit adder.circ as structural Verilog: 1 circuit, main circuit addsubber
module addsubber (
  input  [31:0] A,
  input  [31:0] B,
  input  Subtract,
  output [31:0] Output,
  output Overflow,
  output Carry_Out
);

  wire adder_1_cout, adder_2_cout, adder_3_cout, adder_4_cout, adder_5_cout, adder_6_cout, adder_7_cout,
       adder_8_cout, adder_9_cout, adder_10_cout, adder_11_cout, adder_12_cout, adder_13_cout, adder_14_cout,
       adder_15_cout, adder_16_cout, adder_17_cout, adder_18_cout, adder_19_cout, adder_20_cout,
       adder_21_cout, adder_22_cout, adder_23_cout, adder_24_cout, adder_25_cout, adder_26_cout,
       adder_27_cout, adder_28_cout, adder_29_cout, adder_30_cout, adder_31_cout, xor_1_out, xor_2_out,
       xor_3_out, xor_4_out, xor_5_out, xor_6_out, xor_7_out, xor_8_out, xor_9_out, xor_10_out, xor_11_out,
       xor_12_out, xor_13_out, xor_14_out, xor_15_out, xor_16_out, xor_17_out, xor_18_out, xor_19_out,
       xor_20_out, xor_21_out, xor_22_out, xor_23_out, xor_24_out, xor_25_out, xor_26_out, xor_27_out,
       xor_28_out, xor_29_out, xor_30_out, xor_31_out, xor_32_out;

  xor xor_1 (xor_1_out, Subtract, B[0]);
  xor xor_2 (xor_2_out, Subtract, B[1]);
  xor xor_3 (xor_3_out, Subtract, B[2]);
  xor xor_4 (xor_4_out, Subtract, B[3]);
  xor xor_5 (xor_5_out, Subtract, B[4]);
  xor xor_6 (xor_6_out, Subtract, B[5]);
  xor xor_7 (xor_7_out, Subtract, B[6]);
  xor xor_8 (xor_8_out, Subtract, B[7]);
  xor xor_9 (xor_9_out, Subtract, B[8]);
  xor xor_10 (xor_10_out, Subtract, B[9]);
  xor xor_11 (xor_11_out, Subtract, B[10]);
  xor xor_12 (xor_12_out, Subtract, B[11]);
  xor xor_13 (xor_13_out, Subtract, B[12]);
  xor xor_14 (xor_14_out, Subtract, B[13]);
  xor xor_15 (xor_15_out, Subtract, B[14]);
  xor xor_16 (xor_16_out, Subtract, B[15]);
  xor xor_17 (xor_17_out, Subtract, B[16]);
  xor xor_18 (xor_18_out, Subtract, B[17]);
  xor xor_19 (xor_19_out, Subtract, B[18]);
  xor xor_20 (xor_20_out, Subtract, B[19]);
  xor xor_21 (xor_21_out, Subtract, B[20]);
  xor xor_22 (xor_22_out, Subtract, B[21]);
  xor xor_23 (xor_23_out, Subtract, B[22]);
  xor xor_24 (xor_24_out, Subtract, B[23]);
  xor xor_25 (xor_25_out, Subtract, B[24]);
  xor xor_26 (xor_26_out, Subtract, B[25]);
  xor xor_27 (xor_27_out, Subtract, B[26]);
  xor xor_28 (xor_28_out, Subtract, B[27]);
  xor xor_29 (xor_29_out, Subtract, B[28]);
  xor xor_30 (xor_30_out, Subtract, B[29]);
  xor xor_31 (xor_31_out, Subtract, B[30]);
  xor xor_32 (xor_32_out, Subtract, B[31]);
  Adder #(.width(1)) adder_1 (.a(A[0]), .b(xor_1_out), .out(Output[0]), .cin(Subtract), .cout(adder_1_cout));
  Adder #(.width(1)) adder_2 (.a(A[1]), .b(xor_2_out), .out(Output[1]), .cin(adder_1_cout), .cout(adder_2_cout));
  Adder #(.width(1)) adder_3 (.a(A[2]), .b(xor_3_out), .out(Output[2]), .cin(adder_2_cout), .cout(adder_3_cout));
  Adder #(.width(1)) adder_4 (.a(A[3]), .b(xor_4_out), .out(Output[3]), .cin(adder_3_cout), .cout(adder_4_cout));
  Adder #(.width(1)) adder_5 (.a(A[4]), .b(xor_5_out), .out(Output[4]), .cin(adder_4_cout), .cout(adder_5_cout));
  Adder #(.width(1)) adder_6 (.a(A[5]), .b(xor_6_out), .out(Output[5]), .cin(adder_5_cout), .cout(adder_6_cout));
  Adder #(.width(1)) adder_7 (.a(A[6]), .b(xor_7_out), .out(Output[6]), .cin(adder_6_cout), .cout(adder_7_cout));
  Adder #(.width(1)) adder_8 (.a(A[7]), .b(xor_8_out), .out(Output[7]), .cin(adder_7_cout), .cout(adder_8_cout));
  Adder #(.width(1)) adder_9 (.a(A[8]), .b(xor_9_out), .out(Output[8]), .cin(adder_8_cout), .cout(adder_9_cout));
  Adder #(.width(1)) adder_10 (.a(A[9]), .b(xor_10_out), .out(Output[9]), .cin(adder_9_cout), .cout(adder_10_cout));
  Adder #(.width(1)) adder_11 (.a(A[10]), .b(xor_11_out), .out(Output[10]), .cin(adder_10_cout), .cout(adder_11_cout));
  Adder #(.width(1)) adder_12 (.a(A[11]), .b(xor_12_out), .out(Output[11]), .cin(adder_11_cout), .cout(adder_12_cout));
  Adder #(.width(1)) adder_13 (.a(A[12]), .b(xor_13_out), .out(Output[12]), .cin(adder_12_cout), .cout(adder_13_cout));
  Adder #(.width(1)) adder_14 (.a(A[13]), .b(xor_14_out), .out(Output[13]), .cin(adder_13_cout), .cout(adder_14_cout));
  Adder #(.width(1)) adder_15 (.a(A[14]), .b(xor_15_out), .out(Output[14]), .cin(adder_14_cout), .cout(adder_15_cout));
  Adder #(.width(1)) adder_16 (.a(A[15]), .b(xor_16_out), .out(Output[15]), .cin(adder_15_cout), .cout(adder_16_cout));
  Adder #(.width(1)) adder_17 (.a(A[16]), .b(xor_17_out), .out(Output[16]), .cin(adder_16_cout), .cout(adder_17_cout));
  Adder #(.width(1)) adder_18 (.a(A[17]), .b(xor_18_out), .out(Output[17]), .cin(adder_17_cout), .cout(adder_18_cout));
  Adder #(.width(1)) adder_19 (.a(A[18]), .b(xor_19_out), .out(Output[18]), .cin(adder_18_cout), .cout(adder_19_cout));
  Adder #(.width(1)) adder_20 (.a(A[19]), .b(xor_20_out), .out(Output[19]), .cin(adder_19_cout), .cout(adder_20_cout));
  Adder #(.width(1)) adder_21 (.a(A[20]), .b(xor_21_out), .out(Output[20]), .cin(adder_20_cout), .cout(adder_21_cout));
  Adder #(.width(1)) adder_22 (.a(A[21]), .b(xor_22_out), .out(Output[21]), .cin(adder_21_cout), .cout(adder_22_cout));
  Adder #(.width(1)) adder_23 (.a(A[22]), .b(xor_23_out), .out(Output[22]), .cin(adder_22_cout), .cout(adder_23_cout));
  Adder #(.width(1)) adder_24 (.a(A[23]), .b(xor_24_out), .out(Output[23]), .cin(adder_23_cout), .cout(adder_24_cout));
  Adder #(.width(1)) adder_25 (.a(A[24]), .b(xor_25_out), .out(Output[24]), .cin(adder_24_cout), .cout(adder_25_cout));
  Adder #(.width(1)) adder_26 (.a(A[25]), .b(xor_26_out), .out(Output[25]), .cin(adder_25_cout), .cout(adder_26_cout));
  Adder #(.width(1)) adder_27 (.a(A[26]), .b(xor_27_out), .out(Output[26]), .cin(adder_26_cout), .cout(adder_27_cout));
  Adder #(.width(1)) adder_28 (.a(A[27]), .b(xor_28_out), .out(Output[27]), .cin(adder_27_cout), .cout(adder_28_cout));
  Adder #(.width(1)) adder_29 (.a(A[28]), .b(xor_29_out), .out(Output[28]), .cin(adder_28_cout), .cout(adder_29_cout));
  Adder #(.width(1)) adder_30 (.a(A[29]), .b(xor_30_out), .out(Output[29]), .cin(adder_29_cout), .cout(adder_30_cout));
  Adder #(.width(1)) adder_31 (.a(A[30]), .b(xor_31_out), .out(Output[30]), .cin(adder_30_cout), .cout(adder_31_cout));
  Adder #(.width(1)) adder_32 (.a(A[31]), .b(xor_32_out), .out(Output[31]), .cin(adder_31_cout), .cout(Carry_Out));
  xor xor_33 (Overflow, adder_31_cout, Carry_Out);
endmodule
