// Logisim project alu.circ as structural Verilog: 1 circuit, main circuit ALU
module ALU (
  input  [31:0] A,
  input  [31:0] B,
  input  [3:0] ALUCtrl,
  output [31:0] Output,
  output Carry_out,
  output Overflow,
  output Zero
);

  wire not_1_out, or_1_out, xor_1_out;
  wire [1:0] nand_2_out;
  wire [1:1] and_1_out;
  wire [4:0] bit_extender_1_out;
  wire [31:0] arithmetic_output, bit_extender_2_out, logic_output, shifter_output;

  and and_1 (and_1_out[1], ALUCtrl[1], ALUCtrl[0]);
  Bit_Extender #(.in_width(32), .out_width(5)) bit_extender_1 (.in(A), .out(bit_extender_1_out));
  or or_1 (or_1_out, ALUCtrl[1], ALUCtrl[0]);
  shifter shifter (.Shift_Amount(bit_extender_1_out), .Input(B), .Shift_Op(2'b00), .Output(shifter_output));
  \logic  \logic  (.A(A), .B(B), .Logical_Op({and_1_out[1], ALUCtrl[1]}), .Output(logic_output));
  addsubber arithmetic (
    .B(B), .A(A), .Subtract(or_1_out), .Overflow(Overflow), .Carry_Out(Carry_out), .Output(arithmetic_output));
  xor xor_1 (xor_1_out, arithmetic_output[31], Overflow);
  assign bit_extender_2_out = {{31{1'b0}}, xor_1_out};  // Bit_Extender bit_extender_2
  nand nand_1 (nand_2_out[1], ALUCtrl[2], ALUCtrl[1]);
  Multiplexer #(.select(2), .width(32), .enable("false")) multiplexer_1 (
    .in0(shifter_output), .in1(bit_extender_2_out), .in2(arithmetic_output), .in3(logic_output),
    .out(Output), .sel(nand_2_out));
  nand nand_2 (nand_2_out[0], not_1_out, ALUCtrl[2]);
  not not_1 (not_1_out, ALUCtrl[1]);
  nor nor_1 (Zero, Output[31], Output[30], Output[29], Output[28], Output[27], Output[26], Output[25], Output[24], Output[23], Output[22], Output[21], Output[20], Output[19], Output[18], Output[17], Output[16], Output[14], Output[13], Output[12], Output[11], Output[10], Output[9], Output[8], Output[7], Output[6], Output[5], Output[4], Output[3], Output[2], Output[1], Output[0], Output[15]);
endmodule
