// Logisim project aluctrl.circ as structural Verilog: 2 circuits, main circuit AluCtrl
module AluCtrl (
  input  [5:0] Funct,
  input  [2:0] AluOp,
  output [3:0] AluCtrl
);

  wire decoder_1_out0, decoder_1_out1, decoder_3_out0, decoder_3_out2, decoder_3_out4, decoder_3_out5,
       decoder_3_out6, decoder_3_out10, nor_1_out;
  wire [2:0] createop_1_bit0, multiplexer_1_out;

  Decoder #(.enable("false")) decoder_1 (.out0(decoder_1_out0), .out1(decoder_1_out1), .sel(Funct[5]));
  Decoder #(.select(5), .disabled(0)) decoder_2 (
    .sel(Funct[4:0]), .en(decoder_1_out0));  // open: out0, out1, out2, out3, out4, out5, out6, out7, out8, out9, out10, out11, out12, out13, out14, out15, out16, out17, out18, out19, out20, out21, out22, out23, out24, out25, out26, out27, out28, out29, out30, out31
  Decoder #(.select(5), .disabled(0)) decoder_3 (
    .out0(decoder_3_out0), .out2(decoder_3_out2), .out4(decoder_3_out4), .out5(decoder_3_out5),
    .out6(decoder_3_out6), .out10(decoder_3_out10), .sel(Funct[4:0]), .en(decoder_1_out1));  // open: out1, out3, out7, out8, out9, out11, out12, out13, out14, out15, out16, out17, out18, out19, out20, out21, out22, out23, out24, out25, out26, out27, out28, out29, out30, out31
  CreateOp createop_1 (
    .add(decoder_3_out0), .sub(decoder_3_out2), .\and (decoder_3_out4), .\or (decoder_3_out5),
    .\xor (decoder_3_out6), .slt(decoder_3_out10), .Bit0(createop_1_bit0[0]), .Bit1(createop_1_bit0[1]),
    .Bit2(createop_1_bit0[2]));
  nor nor_1 (nor_1_out, AluOp[0], AluOp[1], AluOp[2]);
  Multiplexer #(.width(3), .enable("false")) multiplexer_1 (
    .in0(AluOp), .in1(createop_1_bit0), .out(multiplexer_1_out), .sel(nor_1_out));
  assign AluCtrl = {{1{1'b0}}, multiplexer_1_out};  // Bit_Extender bit_extender_1

  // Notes on the sheet:
  //   and,or,xor
  //   add
  //   sub
  //   slt
endmodule

module CreateOp (
  input  add,
  input  sub,
  input  \and ,
  input  \or ,
  input  \xor ,
  input  slt,
  output Bit0,
  output Bit1,
  output Bit2
);

  or or_1 (Bit0, \and , \xor , sub);
  or or_2 (Bit1, \or , \xor , slt);
  or or_3 (Bit2, add, sub, slt);
endmodule
