// Logisim project data memory.circ as structural Verilog: 1 circuit, main circuit Data Memory
module Data_Memory (
  input  [31:0] Address,
  input  MemWr,
  input  MemRd,
  input  [31:0] Data_in,
  input  Clock,
  output [31:0] Data_out
);

  RAM #(.addrWidth(24), .dataWidth(32), .bus("separate")) ram_1 (
    .addr(Address[25:2]), .din(Data_in), .data(Data_out), .str(MemWr), .sel(1'b1), .clk(Clock), .ld(MemRd));  // open: clr
endmodule
