// Logisim project datapath.circ as structural Verilog: 1 circuit, main circuit MIPS Datapath
module MIPS_Datapath (
  input  ExtOp,
  input  MemtoReg,
  input  RegDst,
  input  J,
  input  PCSrc,
  input  RegWr,
  input  ALUSrc,
  input  [3:0] AluCtr,
  input  MemWr,
  input  MemRd,
  input  Clock,
  output [5:0] Op,
  output [5:0] func,
  output Zero
);

  wire [4:0] multiplexer_3_out;
  wire [27:0] PC_q;
  wire [29:0] adder_2_out;
  wire [31:0] ALU_output, Data_Memory_data_out, Ext_out_3, multiplexer_1_out, multiplexer_2_out,
       multiplexer_4_out, multiplexer_5_out, register_file_1_busa, register_file_1_busb;
  wire [31:2] adder_1_out;
  wire [31:8] PC_q_2;

  Multiplexer #(.width(32), .enable("false")) multiplexer_1 (
    .in0({adder_1_out, 2'b00}), .in1(multiplexer_2_out), .out(multiplexer_1_out), .sel(PCSrc));
  Multiplexer #(.width(32), .enable("false")) multiplexer_2 (
    .in0({adder_2_out, 2'b00}), .in1({PC_q_2, func, 2'b00}), .out(multiplexer_2_out), .sel(J));
  Register #(.width(32)) PC (.D(multiplexer_1_out), .Q({PC_q_2[31:28], PC_q}), .clk(Clock));  // open: en, clr
  Adder #(.width(30)) adder_1 (.a(30'h1), .b({PC_q_2[31:28], PC_q[27:2]}), .out(adder_1_out));  // open: cin, cout
  Instruction_Memory Instruction_Memory (.Address({PC_q_2[31:28], PC_q}), .Output({Op, PC_q_2[27:8], func}));
  Extender Ext (.Imm16({PC_q_2[17:8], func}), .ExtOp(ExtOp), .out_3(Ext_out_3));
  Register_File register_file_1 (
    .RA(PC_q_2[27:23]), .RB(PC_q_2[22:18]), .RW(multiplexer_3_out), .BusW(multiplexer_5_out), .RegWr(RegWr),
    .Clock(Clock), .BusA(register_file_1_busa), .BusB(register_file_1_busb));  // open: Clear
  Multiplexer #(.width(5), .enable("false")) multiplexer_3 (
    .in0(PC_q_2[22:18]), .in1(PC_q_2[17:13]), .out(multiplexer_3_out), .sel(RegDst));
  Multiplexer #(.width(32), .enable("false")) multiplexer_4 (
    .in0(register_file_1_busb), .in1(Ext_out_3), .out(multiplexer_4_out), .sel(ALUSrc));
  Adder #(.width(30)) adder_2 (.a(adder_1_out), .b(Ext_out_3[29:0]), .out(adder_2_out));  // open: cin, cout
  ALU ALU (
    .A(register_file_1_busa), .B(multiplexer_4_out), .ALUCtrl(AluCtr), .Zero(Zero), .Output(ALU_output));  // open: Carry_out, Overflow
  Data_Memory Data_Memory (
    .Address(ALU_output), .Data_in(register_file_1_busb), .MemWr(MemWr), .Clock(Clock), .MemRd(MemRd),
    .Data_out(Data_Memory_data_out));
  Multiplexer #(.width(32), .enable("false")) multiplexer_5 (
    .in0(ALU_output), .in1(Data_Memory_data_out), .out(multiplexer_5_out), .sel(MemtoReg));
endmodule
