// Logisim project extender.circ as structural Verilog: 1 circuit, main circuit Extender
module Extender (
  input  [15:0] Imm16,
  input  ExtOp,
  output [31:0] out_3
);

  wire [31:0] bit_extender_1_out, bit_extender_2_out;

  assign bit_extender_1_out = {{16{1'b0}}, Imm16};  // Bit_Extender bit_extender_1
  Multiplexer #(.width(32), .enable("false")) multiplexer_1 (
    .in0(bit_extender_1_out), .in1(bit_extender_2_out), .out(out_3), .sel(ExtOp));
  assign bit_extender_2_out = {{16{Imm16[15]}}, Imm16};  // Bit_Extender bit_extender_2
endmodule
