// Logisim project instruction memory.circ as structural Verilog: 1 circuit, main circuit Instruction Memory
module Instruction_Memory (
  input  [31:0] Address,
  output [31:0] Output
);

  ROM #(.addrWidth(24), .dataWidth(32)) rom_1 (.addr(Address[25:2]), .data(Output));  // open: sel
endmodule
