// Logisim project logicops.circ as structural Verilog: 1 circuit, main circuit logic
module \logic  (
  input  [31:0] A,
  input  [31:0] B,
  input  [1:0] Logical_Op,
  output [31:0] Output
);

  wire [31:0] and_1_out, not_1_out, or_1_out, xor_1_out;

  assign and_1_out = A & B;  // AND_Gate and_1, 32 bits wide
  assign or_1_out = A | B;  // OR_Gate or_1, 32 bits wide
  assign xor_1_out = A ^ B;  // XOR_Gate xor_1, 32 bits wide
  assign not_1_out = ~or_1_out;  // NOT_Gate not_1, 32 bits wide
  Multiplexer #(.select(2), .width(32), .enable("false")) multiplexer_1 (
    .in0(and_1_out), .in1(or_1_out), .in2(not_1_out), .in3(xor_1_out), .out(Output), .sel(Logical_Op));
endmodule
