// Logisim project maincontrol.circ as structural Verilog: 2 circuits, main circuit Main Control
module Main_Control (
  input  [5:0] Op,
  output [2:0] AluOp,
  output RegDst,
  output RegWrite,
  output ExtOp,
  output ALUSrc,
  output Beq,
  output Bne,
  output J,
  output MemRead,
  output MemWrite,
  output MemtoReg
);

  wire decoder_1_out0, decoder_1_out1, decoder_2_out8, decoder_2_out10, decoder_2_out12, decoder_2_out13,
       decoder_2_out14;

  Decoder #(.enable("false")) decoder_1 (.out0(decoder_1_out0), .out1(decoder_1_out1), .sel(Op[5]));
  Decoder #(.select(5), .disabled(0)) decoder_2 (
    .out0(RegDst), .out2(J), .out4(Beq), .out5(Bne), .out8(decoder_2_out8), .out10(decoder_2_out10),
    .out12(decoder_2_out12), .out13(decoder_2_out13), .out14(decoder_2_out14), .sel(Op[4:0]),
    .en(decoder_1_out0));  // open: out1, out3, out6, out7, out9, out11, out15, out16, out17, out18, out19, out20, out21, out22, out23, out24, out25, out26, out27, out28, out29, out30, out31
  Decoder #(.select(5), .disabled(0)) decoder_3 (
    .out3(MemRead), .out11(MemWrite), .sel(Op[4:0]), .en(decoder_1_out1));  // open: out0, out1, out2, out4, out5, out6, out7, out8, out9, out10, out12, out13, out14, out15, out16, out17, out18, out19, out20, out21, out22, out23, out24, out25, out26, out27, out28, out29, out30, out31
  nor nor_1 (RegWrite, MemWrite, Beq, Bne, J);
  nor nor_2 (ExtOp, decoder_2_out12, decoder_2_out13, decoder_2_out14);
  nor nor_3 (ALUSrc, RegDst, Beq, Bne);
  aluop aluop_1 (
    .rtype(RegDst), .andi(decoder_2_out12), .ori(decoder_2_out13), .xori(decoder_2_out14), .lw(MemRead),
    .sw(MemWrite), .beq(Beq), .bne(Bne), .j(J), .addi(decoder_2_out8), .slti(decoder_2_out10),
    .AluOp0(AluOp[0]), .AluOp1(AluOp[1]), .AluOp2(AluOp[2]));

  assign MemtoReg = MemRead;

  // Notes on the sheet:
  //   addi
  //   slti
  //   rtype
  //   xori
  //   lw
  //   j
  //   andi
  //   ori
  //   sw
  //   beq
  //   bne
endmodule

module aluop (
  input  rtype,
  input  andi,
  input  ori,
  input  xori,
  input  lw,
  input  sw,
  input  beq,
  input  bne,
  input  j,
  input  addi,
  input  slti,
  output AluOp0,
  output AluOp1,
  output AluOp2
);

  or or_1 (AluOp0, andi, xori, beq, bne);
  or or_2 (AluOp1, slti, ori, xori);
  or or_3 (AluOp2, addi, slti, lw, sw, beq, bne);
endmodule
