// Logisim project pcsrccontrol.circ as structural Verilog: 1 circuit, main circuit PCSrcControl
module PCSrcControl (
  input  J,
  input  Beq,
  input  Zero,
  input  Bne,
  output PCSrc
);

  wire and_1_out, and_2_out, not_1_out;

  and and_1 (and_1_out, Beq, Zero);
  and and_2 (and_2_out, Bne, not_1_out);
  not not_1 (not_1_out, Zero);
  or or_1 (PCSrc, J, and_1_out, and_2_out);
endmodule
