// Logisim project processor.circ as structural Verilog: 1 circuit, main circuit main
module main (
);

  wire clock_1_out, main_control_1_alusrc, main_control_1_beq, main_control_1_bne, main_control_1_extop,
       main_control_1_j, main_control_1_memread, main_control_1_memtoreg, main_control_1_memwrite,
       main_control_1_regdst, main_control_1_regwrite, mips_datapath_1_zero, pcsrccontrol_1_pcsrc;
  wire [2:0] main_control_1_aluop;
  wire [3:0] aluctrl_1_aluctrl;
  wire [5:0] mips_datapath_1_func, mips_datapath_1_op;

  PCSrcControl pcsrccontrol_1 (
    .J(main_control_1_j), .Beq(main_control_1_beq), .Zero(mips_datapath_1_zero), .Bne(main_control_1_bne),
    .PCSrc(pcsrccontrol_1_pcsrc));
  Clock clock_1 (.out(clock_1_out));
  MIPS_Datapath mips_datapath_1 (
    .J(main_control_1_j), .PCSrc(pcsrccontrol_1_pcsrc), .Clock(clock_1_out), .Op(mips_datapath_1_op),
    .func(mips_datapath_1_func), .ExtOp(main_control_1_extop), .RegDst(main_control_1_regdst),
    .RegWr(main_control_1_regwrite), .ALUSrc(main_control_1_alusrc), .AluCtr(aluctrl_1_aluctrl),
    .Zero(mips_datapath_1_zero), .MemWr(main_control_1_memwrite), .MemRd(main_control_1_memread),
    .MemtoReg(main_control_1_memtoreg));
  Main_Control main_control_1 (
    .Op(mips_datapath_1_op), .AluOp(main_control_1_aluop), .RegDst(main_control_1_regdst),
    .RegWrite(main_control_1_regwrite), .ExtOp(main_control_1_extop), .ALUSrc(main_control_1_alusrc),
    .Beq(main_control_1_beq), .Bne(main_control_1_bne), .J(main_control_1_j),
    .MemRead(main_control_1_memread), .MemWrite(main_control_1_memwrite), .MemtoReg(main_control_1_memtoreg));
  AluCtrl aluctrl_1 (.Funct(mips_datapath_1_func), .AluOp(main_control_1_aluop), .AluCtrl(aluctrl_1_aluctrl));
endmodule
