// Logisim project registers.circ as structural Verilog: 1 circuit, main circuit Register File
module Register_File (
  input  [4:0] RA,
  input  [4:0] RB,
  input  [4:0] RW,
  input  Clock,
  input  Clear,
  input  RegWr,
  input  [31:0] BusW,
  output [31:0] BusA,
  output [31:0] BusB
);

  wire and_1_out, and_2_out, and_3_out, and_4_out, and_5_out, and_6_out, and_7_out, and_8_out, and_9_out,
       and_10_out, and_11_out, and_12_out, and_13_out, and_14_out, and_15_out, and_16_out, and_17_out,
       and_18_out, and_19_out, and_20_out, and_21_out, and_22_out, and_23_out, and_24_out, and_25_out,
       and_26_out, and_27_out, and_28_out, and_29_out, and_30_out, and_31_out, decoder_1_out1,
       decoder_1_out2, decoder_1_out3, decoder_1_out4, decoder_1_out5, decoder_1_out6, decoder_1_out7,
       decoder_1_out8, decoder_1_out9, decoder_1_out10, decoder_1_out11, decoder_1_out12, decoder_1_out13,
       decoder_1_out14, decoder_1_out15, decoder_1_out16, decoder_1_out17, decoder_1_out18, decoder_1_out19,
       decoder_1_out20, decoder_1_out21, decoder_1_out22, decoder_1_out23, decoder_1_out24, decoder_1_out25,
       decoder_1_out26, decoder_1_out27, decoder_1_out28, decoder_1_out29, decoder_1_out30, decoder_1_out31,
       decoder_2_out0, decoder_2_out1, decoder_2_out2, decoder_2_out3, decoder_2_out4, decoder_2_out5,
       decoder_2_out6, decoder_2_out7, decoder_2_out8, decoder_2_out9, decoder_2_out10, decoder_2_out11,
       decoder_2_out12, decoder_2_out13, decoder_2_out14, decoder_2_out15, decoder_2_out16, decoder_2_out17,
       decoder_2_out18, decoder_2_out19, decoder_2_out20, decoder_2_out21, decoder_2_out22, decoder_2_out23,
       decoder_2_out24, decoder_2_out25, decoder_2_out26, decoder_2_out27, decoder_2_out28, decoder_2_out29,
       decoder_2_out30, decoder_2_out31, decoder_3_out0, decoder_3_out1, decoder_3_out2, decoder_3_out3,
       decoder_3_out4, decoder_3_out5, decoder_3_out6, decoder_3_out7, decoder_3_out8, decoder_3_out9,
       decoder_3_out10, decoder_3_out11, decoder_3_out12, decoder_3_out13, decoder_3_out14, decoder_3_out15,
       decoder_3_out16, decoder_3_out17, decoder_3_out18, decoder_3_out19, decoder_3_out20, decoder_3_out21,
       decoder_3_out22, decoder_3_out23, decoder_3_out24, decoder_3_out25, decoder_3_out26, decoder_3_out27,
       decoder_3_out28, decoder_3_out29, decoder_3_out30, decoder_3_out31;
  wire [31:0] a0_q, a1_q, a2_q, a3_q, fp_q, gp_q, k0_q, k1_q, ra_q, s0_q, s1_q, s2_q, s3_q, s4_q, s5_q, s6_q,
       s7_q, sp_q, t0_q, t1_q, t2_q, t3_q, t4_q, t5_q, t6_q, t7_q, t8_q, t9_q, v0_q, v1_q;

  Decoder #(.select(5)) decoder_1 (
    .out1(decoder_1_out1), .out2(decoder_1_out2), .out3(decoder_1_out3), .out4(decoder_1_out4),
    .out5(decoder_1_out5), .out6(decoder_1_out6), .out7(decoder_1_out7), .out8(decoder_1_out8),
    .out9(decoder_1_out9), .out10(decoder_1_out10), .out11(decoder_1_out11), .out12(decoder_1_out12),
    .out13(decoder_1_out13), .out14(decoder_1_out14), .out15(decoder_1_out15), .out16(decoder_1_out16),
    .out17(decoder_1_out17), .out18(decoder_1_out18), .out19(decoder_1_out19), .out20(decoder_1_out20),
    .out21(decoder_1_out21), .out22(decoder_1_out22), .out23(decoder_1_out23), .out24(decoder_1_out24),
    .out25(decoder_1_out25), .out26(decoder_1_out26), .out27(decoder_1_out27), .out28(decoder_1_out28),
    .out29(decoder_1_out29), .out30(decoder_1_out30), .out31(decoder_1_out31), .sel(RW));  // open: out0, en
  and and_1 (and_1_out, RegWr, decoder_1_out1);
  and and_2 (and_2_out, RegWr, decoder_1_out2);
  and and_3 (and_3_out, RegWr, decoder_1_out3);
  and and_4 (and_4_out, RegWr, decoder_1_out4);
  and and_5 (and_5_out, RegWr, decoder_1_out5);
  and and_6 (and_6_out, RegWr, decoder_1_out6);
  and and_7 (and_7_out, RegWr, decoder_1_out7);
  and and_8 (and_8_out, RegWr, decoder_1_out8);
  and and_9 (and_9_out, RegWr, decoder_1_out9);
  and and_10 (and_10_out, RegWr, decoder_1_out10);
  and and_11 (and_11_out, RegWr, decoder_1_out11);
  and and_12 (and_12_out, RegWr, decoder_1_out12);
  and and_13 (and_13_out, RegWr, decoder_1_out13);
  and and_14 (and_14_out, RegWr, decoder_1_out14);
  and and_15 (and_15_out, RegWr, decoder_1_out15);
  and and_16 (and_16_out, RegWr, decoder_1_out16);
  and and_17 (and_17_out, RegWr, decoder_1_out17);
  and and_18 (and_18_out, RegWr, decoder_1_out18);
  and and_19 (and_19_out, RegWr, decoder_1_out19);
  and and_20 (and_20_out, RegWr, decoder_1_out20);
  and and_21 (and_21_out, RegWr, decoder_1_out21);
  and and_22 (and_22_out, RegWr, decoder_1_out22);
  and and_23 (and_23_out, RegWr, decoder_1_out23);
  and and_24 (and_24_out, RegWr, decoder_1_out24);
  and and_25 (and_25_out, RegWr, decoder_1_out25);
  and and_26 (and_26_out, RegWr, decoder_1_out26);
  and and_27 (and_27_out, RegWr, decoder_1_out27);
  and and_28 (and_28_out, RegWr, decoder_1_out28);
  and and_29 (and_29_out, RegWr, decoder_1_out29);
  and and_30 (and_30_out, RegWr, decoder_1_out30);
  and and_31 (and_31_out, RegWr, decoder_1_out31);
  assign BusA = decoder_2_out0 ? {32{1'b0}} : 32'bz;  // Controlled_Buffer controlled_buffer_1
  assign BusA = decoder_2_out1 ? BusW : 32'bz;  // Controlled_Buffer controlled_buffer_2
  Register #(.width(32)) at (.en(and_1_out), .clk(Clock), .clr(Clear));  // open: D, Q
  Register #(.width(32)) v0 (.D(BusW), .en(and_2_out), .Q(v0_q), .clr(Clear));  // open: clk
  Register #(.width(32)) v1 (.D(BusW), .en(and_3_out), .Q(v1_q), .clk(Clock), .clr(Clear));
  Register #(.width(32)) a0 (.D(BusW), .en(and_4_out), .Q(a0_q), .clk(Clock), .clr(Clear));
  Register #(.width(32)) a1 (.D(BusW), .en(and_5_out), .Q(a1_q), .clk(Clock), .clr(Clear));
  Register #(.width(32)) a2 (.D(BusW), .en(and_6_out), .Q(a2_q), .clk(Clock), .clr(Clear));
  Register #(.width(32)) a3 (.D(BusW), .en(and_7_out), .Q(a3_q), .clk(Clock), .clr(Clear));
  Register #(.width(32)) t0 (.D(BusW), .en(and_8_out), .Q(t0_q), .clk(Clock), .clr(Clear));
  Register #(.width(32)) t1 (.D(BusW), .en(and_9_out), .Q(t1_q), .clk(Clock), .clr(Clear));
  Register #(.width(32)) t2 (.D(BusW), .en(and_10_out), .Q(t2_q), .clk(Clock), .clr(Clear));
  Register #(.width(32)) t3 (.D(BusW), .en(and_11_out), .Q(t3_q), .clk(Clock), .clr(Clear));
  Register #(.width(32)) t4 (.D(BusW), .en(and_12_out), .Q(t4_q), .clk(Clock), .clr(Clear));
  Register #(.width(32)) t5 (.D(BusW), .en(and_13_out), .Q(t5_q), .clk(Clock), .clr(Clear));
  Register #(.width(32)) t6 (.D(BusW), .en(and_14_out), .Q(t6_q), .clk(Clock), .clr(Clear));
  Register #(.width(32)) t7 (.D(BusW), .en(and_15_out), .Q(t7_q), .clk(Clock), .clr(Clear));
  Register #(.width(32)) s0 (.D(BusW), .en(and_16_out), .Q(s0_q), .clk(Clock), .clr(Clear));
  Register #(.width(32)) s1 (.D(BusW), .en(and_17_out), .Q(s1_q), .clk(Clock), .clr(Clear));
  Register #(.width(32)) s2 (.D(BusW), .en(and_18_out), .Q(s2_q), .clk(Clock), .clr(Clear));
  Register #(.width(32)) s3 (.D(BusW), .en(and_19_out), .Q(s3_q), .clk(Clock), .clr(Clear));
  Register #(.width(32)) s4 (.D(BusW), .en(and_20_out), .Q(s4_q), .clk(Clock), .clr(Clear));
  Register #(.width(32)) s5 (.D(BusW), .en(and_21_out), .Q(s5_q), .clk(Clock), .clr(Clear));
  Register #(.width(32)) s6 (.D(BusW), .en(and_22_out), .Q(s6_q), .clk(Clock), .clr(Clear));
  Register #(.width(32)) s7 (.D(BusW), .en(and_23_out), .Q(s7_q), .clk(Clock), .clr(Clear));
  Register #(.width(32)) t8 (.D(BusW), .en(and_24_out), .Q(t8_q), .clk(Clock), .clr(Clear));
  Register #(.width(32)) t9 (.D(BusW), .en(and_25_out), .Q(t9_q), .clk(Clock), .clr(Clear));
  Register #(.width(32)) k0 (.D(BusW), .en(and_26_out), .Q(k0_q), .clk(Clock), .clr(Clear));
  Register #(.width(32)) k1 (.D(BusW), .en(and_27_out), .Q(k1_q), .clk(Clock), .clr(Clear));
  Register #(.width(32)) gp (.D(BusW), .en(and_28_out), .Q(gp_q), .clk(Clock), .clr(Clear));
  Register #(.width(32)) sp (.D(BusW), .en(and_29_out), .Q(sp_q), .clk(Clock), .clr(Clear));
  Register #(.width(32)) fp (.D(BusW), .en(and_30_out), .Q(fp_q), .clk(Clock), .clr(Clear));
  Register #(.width(32)) u_ra (.D(BusW), .en(and_31_out), .Q(ra_q), .clk(Clock), .clr(Clear));
  assign BusA = decoder_2_out2 ? v0_q : 32'bz;  // Controlled_Buffer controlled_buffer_3
  assign BusA = decoder_2_out3 ? v1_q : 32'bz;  // Controlled_Buffer controlled_buffer_4
  assign BusA = decoder_2_out4 ? a0_q : 32'bz;  // Controlled_Buffer controlled_buffer_5
  assign BusA = decoder_2_out5 ? a1_q : 32'bz;  // Controlled_Buffer controlled_buffer_6
  Decoder #(.select(5)) decoder_2 (
    .out0(decoder_2_out0), .out1(decoder_2_out1), .out2(decoder_2_out2), .out3(decoder_2_out3),
    .out4(decoder_2_out4), .out5(decoder_2_out5), .out6(decoder_2_out6), .out7(decoder_2_out7),
    .out8(decoder_2_out8), .out9(decoder_2_out9), .out10(decoder_2_out10), .out11(decoder_2_out11),
    .out12(decoder_2_out12), .out13(decoder_2_out13), .out14(decoder_2_out14), .out15(decoder_2_out15),
    .out16(decoder_2_out16), .out17(decoder_2_out17), .out18(decoder_2_out18), .out19(decoder_2_out19),
    .out20(decoder_2_out20), .out21(decoder_2_out21), .out22(decoder_2_out22), .out23(decoder_2_out23),
    .out24(decoder_2_out24), .out25(decoder_2_out25), .out26(decoder_2_out26), .out27(decoder_2_out27),
    .out28(decoder_2_out28), .out29(decoder_2_out29), .out30(decoder_2_out30), .out31(decoder_2_out31),
    .sel(RA), .en(1'b1));
  assign BusA = decoder_2_out6 ? a2_q : 32'bz;  // Controlled_Buffer controlled_buffer_7
  assign BusA = decoder_2_out7 ? a3_q : 32'bz;  // Controlled_Buffer controlled_buffer_8
  assign BusA = decoder_2_out8 ? t0_q : 32'bz;  // Controlled_Buffer controlled_buffer_9
  assign BusA = decoder_2_out9 ? t1_q : 32'bz;  // Controlled_Buffer controlled_buffer_10
  assign BusA = decoder_2_out10 ? t2_q : 32'bz;  // Controlled_Buffer controlled_buffer_11
  assign BusA = decoder_2_out11 ? t3_q : 32'bz;  // Controlled_Buffer controlled_buffer_12
  assign BusA = decoder_2_out12 ? t4_q : 32'bz;  // Controlled_Buffer controlled_buffer_13
  assign BusA = decoder_2_out13 ? t5_q : 32'bz;  // Controlled_Buffer controlled_buffer_14
  assign BusA = decoder_2_out14 ? t6_q : 32'bz;  // Controlled_Buffer controlled_buffer_15
  assign BusA = decoder_2_out15 ? t7_q : 32'bz;  // Controlled_Buffer controlled_buffer_16
  assign BusA = decoder_2_out16 ? s0_q : 32'bz;  // Controlled_Buffer controlled_buffer_17
  assign BusA = decoder_2_out17 ? s1_q : 32'bz;  // Controlled_Buffer controlled_buffer_18
  assign BusA = decoder_2_out18 ? s2_q : 32'bz;  // Controlled_Buffer controlled_buffer_19
  assign BusA = decoder_2_out19 ? s3_q : 32'bz;  // Controlled_Buffer controlled_buffer_20
  assign BusA = decoder_2_out20 ? s4_q : 32'bz;  // Controlled_Buffer controlled_buffer_21
  assign BusA = decoder_2_out21 ? s5_q : 32'bz;  // Controlled_Buffer controlled_buffer_22
  assign BusA = decoder_2_out22 ? s6_q : 32'bz;  // Controlled_Buffer controlled_buffer_23
  assign BusA = decoder_2_out23 ? s7_q : 32'bz;  // Controlled_Buffer controlled_buffer_24
  assign BusA = decoder_2_out24 ? t8_q : 32'bz;  // Controlled_Buffer controlled_buffer_25
  assign BusA = decoder_2_out25 ? t9_q : 32'bz;  // Controlled_Buffer controlled_buffer_26
  assign BusA = decoder_2_out26 ? k0_q : 32'bz;  // Controlled_Buffer controlled_buffer_27
  assign BusA = decoder_2_out27 ? k1_q : 32'bz;  // Controlled_Buffer controlled_buffer_28
  assign BusA = decoder_2_out28 ? gp_q : 32'bz;  // Controlled_Buffer controlled_buffer_29
  assign BusA = decoder_2_out29 ? sp_q : 32'bz;  // Controlled_Buffer controlled_buffer_30
  assign BusA = decoder_2_out30 ? fp_q : 32'bz;  // Controlled_Buffer controlled_buffer_31
  assign BusA = decoder_2_out31 ? ra_q : 32'bz;  // Controlled_Buffer controlled_buffer_32
  assign BusB = decoder_3_out0 ? {32{1'b0}} : 32'bz;  // Controlled_Buffer controlled_buffer_33
  assign BusB = decoder_3_out1 ? BusW : 32'bz;  // Controlled_Buffer controlled_buffer_34
  assign BusB = decoder_3_out2 ? v0_q : 32'bz;  // Controlled_Buffer controlled_buffer_35
  assign BusB = decoder_3_out3 ? v1_q : 32'bz;  // Controlled_Buffer controlled_buffer_36
  assign BusB = decoder_3_out4 ? a0_q : 32'bz;  // Controlled_Buffer controlled_buffer_37
  Decoder #(.select(5)) decoder_3 (
    .out0(decoder_3_out0), .out1(decoder_3_out1), .out2(decoder_3_out2), .out3(decoder_3_out3),
    .out4(decoder_3_out4), .out5(decoder_3_out5), .out6(decoder_3_out6), .out7(decoder_3_out7),
    .out8(decoder_3_out8), .out9(decoder_3_out9), .out10(decoder_3_out10), .out11(decoder_3_out11),
    .out12(decoder_3_out12), .out13(decoder_3_out13), .out14(decoder_3_out14), .out15(decoder_3_out15),
    .out16(decoder_3_out16), .out17(decoder_3_out17), .out18(decoder_3_out18), .out19(decoder_3_out19),
    .out20(decoder_3_out20), .out21(decoder_3_out21), .out22(decoder_3_out22), .out23(decoder_3_out23),
    .out24(decoder_3_out24), .out25(decoder_3_out25), .out26(decoder_3_out26), .out27(decoder_3_out27),
    .out28(decoder_3_out28), .out29(decoder_3_out29), .out30(decoder_3_out30), .out31(decoder_3_out31),
    .sel(RB), .en(1'b1));
  assign BusB = decoder_3_out5 ? a1_q : 32'bz;  // Controlled_Buffer controlled_buffer_38
  assign BusB = decoder_3_out6 ? a2_q : 32'bz;  // Controlled_Buffer controlled_buffer_39
  assign BusB = decoder_3_out7 ? a3_q : 32'bz;  // Controlled_Buffer controlled_buffer_40
  assign BusB = decoder_3_out8 ? t0_q : 32'bz;  // Controlled_Buffer controlled_buffer_41
  assign BusB = decoder_3_out9 ? t1_q : 32'bz;  // Controlled_Buffer controlled_buffer_42
  assign BusB = decoder_3_out10 ? t2_q : 32'bz;  // Controlled_Buffer controlled_buffer_43
  assign BusB = decoder_3_out11 ? t3_q : 32'bz;  // Controlled_Buffer controlled_buffer_44
  assign BusB = decoder_3_out12 ? t4_q : 32'bz;  // Controlled_Buffer controlled_buffer_45
  assign BusB = decoder_3_out13 ? t5_q : 32'bz;  // Controlled_Buffer controlled_buffer_46
  assign BusB = decoder_3_out14 ? t6_q : 32'bz;  // Controlled_Buffer controlled_buffer_47
  assign BusB = decoder_3_out15 ? t7_q : 32'bz;  // Controlled_Buffer controlled_buffer_48
  assign BusB = decoder_3_out16 ? s0_q : 32'bz;  // Controlled_Buffer controlled_buffer_49
  assign BusB = decoder_3_out17 ? s1_q : 32'bz;  // Controlled_Buffer controlled_buffer_50
  assign BusB = decoder_3_out18 ? s2_q : 32'bz;  // Controlled_Buffer controlled_buffer_51
  assign BusB = decoder_3_out19 ? s3_q : 32'bz;  // Controlled_Buffer controlled_buffer_52
  assign BusB = decoder_3_out20 ? s4_q : 32'bz;  // Controlled_Buffer controlled_buffer_53
  assign BusB = decoder_3_out21 ? s5_q : 32'bz;  // Controlled_Buffer controlled_buffer_54
  assign BusB = decoder_3_out22 ? s6_q : 32'bz;  // Controlled_Buffer controlled_buffer_55
  assign BusB = decoder_3_out23 ? s7_q : 32'bz;  // Controlled_Buffer controlled_buffer_56
  assign BusB = decoder_3_out24 ? t8_q : 32'bz;  // Controlled_Buffer controlled_buffer_57
  assign BusB = decoder_3_out25 ? t9_q : 32'bz;  // Controlled_Buffer controlled_buffer_58
  assign BusB = decoder_3_out26 ? k0_q : 32'bz;  // Controlled_Buffer controlled_buffer_59
  assign BusB = decoder_3_out27 ? k1_q : 32'bz;  // Controlled_Buffer controlled_buffer_60
  assign BusB = decoder_3_out28 ? gp_q : 32'bz;  // Controlled_Buffer controlled_buffer_61
  assign BusB = decoder_3_out29 ? sp_q : 32'bz;  // Controlled_Buffer controlled_buffer_62
  assign BusB = decoder_3_out30 ? fp_q : 32'bz;  // Controlled_Buffer controlled_buffer_63
  assign BusB = decoder_3_out31 ? ra_q : 32'bz;  // Controlled_Buffer controlled_buffer_64

  // Notes on the sheet:
  //   $zero
endmodule
