// Logisim project shifter.circ as structural Verilog: 1 circuit, main circuit shifter
module shifter (
  input  [4:0] Shift_Amount,
  input  [1:0] Shift_Op,
  input  [31:0] Input,
  output [31:0] Output
);

  wire [31:0] shifter_1_out, shifter_2_out, shifter_3_out;

  Shifter #(.width(32)) shifter_1 (.in(Input), .\dist (Shift_Amount), .out(shifter_1_out));
  Shifter #(.width(32), .shift("lr")) shifter_2 (.in(Input), .\dist (Shift_Amount), .out(shifter_2_out));
  Shifter #(.width(32), .shift("ar")) shifter_3 (.in(Input), .\dist (Shift_Amount), .out(shifter_3_out));
  Multiplexer #(.select(2), .width(32), .enable("false")) multiplexer_1 (
    .in0(Input), .in1(shifter_1_out), .in2(shifter_2_out), .in3(shifter_3_out), .out(Output), .sel(Shift_Op));
endmodule
